# Fritzing sketch arduino_breadboard_blink (saved by Fritzing 0.8.7b)
circuit board: 6.13292cm x 5.19602cm
breadboards: 1

parts:
  R1 = Resistor [tolerance=±5% resistance=330 package=THT]
  R2 = Resistor [tolerance=±5% resistance=10k package=THT]
  R3 = Resistor [tolerance=±5% resistance=10k package=THT]
  C1 = Ceramic Capacitor [capacitance=22pF package="100 mil [THT, multilayer]"]
  C2 = Ceramic Capacitor [capacitance=22pF package="100 mil [THT, multilayer]"]
  C3 = Electrolytic Capacitor [capacitance=10µF package="100 mil [THT, electrolytic]"]
  C4 = Electrolytic Capacitor [capacitance=10µF package="100 mil [THT, electrolytic]"]
  U2 = Voltage Regulator - 3.3V [part_number=MCP1285 package=TO220-5]
  XTAL1 = Crystal [frequency="16 Mhz" package=THT]
  LED1 = LED - 5mm [color="Yellow (595nm)" package="5 mm [THT]"]
  U3 = LIPO-1000mAh [package=lipo-1000]  # not connected
  Part1 = FTDI Basic Programmer
  U1 = atmega328 [package=dip]
  C5 = Ceramic Capacitor [capacitance=100nF package="100 mil [THT, multilayer]"]  # not connected

nets (from the pcb view):
  N1: R1.Pin_0, LED1.cathode
  GND: R1.Pin_1, C1.1, C2.1, C3.-, C4.-, U2.GND, Part1.GND, U1.GND
  N2: R2.Pin_0, C3.+, U2.input_voltage
  N3: R2.Pin_1, U2.shut_down
  N4: R3.Pin_0, C4.+, U2.output_voltage, Part1.POWER, U1.VCC, U1.AVCC, U1.AREF
  N5: R3.Pin_1, Part1.DTR, U1.RESET
  N6: C1.0, XTAL1.pin_1, U1.XLAT2
  N7: C2.0, XTAL1.pin_0, U1.XLAT1
  N8: LED1.anode, U1.D13
  N9: Part1.RXI, U1.D1_(TX)
  N10: Part1.TXO, U1.D0_(RX)

notes:
  Use the FTDI Breakout only for programming, without battery

custom parts:
  Voltage Regulator - 3.3V: 3.3V DC Voltage Regulator
